# Fritzing sketch umidino (saved by Fritzing 0.9.0b)
perfboards: 1

parts:
  U2 = atmega328 [package=dip]
  Y1 = CRYSTAL [package=crystal-smd-10.5x4.8-2pin]
  V1 = DC Power [voltage=5]
  C1 = Capacitor [package=cap-pth-small2]
  C2 = Capacitor [package=cap-pth-small2]
  JP1 = Header 2 [package=screwterminal-3.5mm-2_lock]
  LCD1 = LCD screen  # not connected

nets:
  N1: U2.D4, V1.V-
  N2: U2.VCC, JP1.2
  N3: U2.GND#7, C1.2, C2.2, JP1.1
  N4: U2.XLAT1, Y1.2, C1.1
  N5: U2.XLAT2, Y1.1, C2.1
